// Digital circuit one_bit_mux.dig as structural Verilog
module one_bit_mux (
  input  a,
  input  s,
  input  b,
  output y
);

  wire and_1_out, and_2_out, not_1_out;

  not not_1 (not_1_out, s);
  and and_1 (and_1_out, a, not_1_out);
  and and_2 (and_2_out, s, b);
  or or_1 (y, and_1_out, and_2_out);
endmodule
